# Fritzing sketch base board v3 (saved by Fritzing 0.9.3b)
circuit board: 7.54664cm x 4.75559cm
stripboards: 1

parts:
  Part1 = Arduino Nano (Rev3.0)
  ThO = female pin header, 1 pin [form="♀ (female)"]
  BT = female pin header, 4 pins [form="♀ (female)"]
  Sharp = female pin header, 3 pins [form="♀ (female)"]
  RL = IC, DIP package, 16 pins [chip_label=IC]
  US = female pin header, 4 pins [form="♀ (female)"]
  SRV = female pin header, 3 pins [form="♀ (female)"]
  RTh = female pin header, 1 pin [form="♀ (female)"]
  LSM = female pin header, 7 pins [form="♀ (female)"]
  Gyro = female pin header, 9 pins [form="♀ (female)"]

nets:
  N1: Part1.D1/TX, BT.pin4
  N2: Part1.D0/RX, BT.pin3
  N3: Part1.GND, BT.pin2, Sharp.pin3, RL.pin1, US.pin4, SRV.pin3, LSM.pin2, Gyro.pin3
  N4: Part1.D3, SRV.pin1
  N5: Part1.D7, US.pin3
  N6: Part1.D8, US.pin2
  N7: Part1.D11/MOSI, RL.pin16
  N8: Part1.D12/MISO, RL.pin11
  N9: Part1.5V, BT.pin1, Sharp.pin2, US.pin1, SRV.pin2, LSM.pin1, Gyro.pin1
  N10: Part1.A5, LSM.pin7, Gyro.pin9
  N11: Part1.A4, LSM.pin6, Gyro.pin8
  N12: Part1.A0, Sharp.pin1
  N13: ThO.pin1, RL.pin13
  N14: RL.pin9, RTh.pin1
